// Logisim project GatesusingotherGates.circ as structural Verilog: 1 circuit, main circuit main
module main (
  input  in_1,
  input  in_2,
  input  in_3,
  input  in_4,
  input  in_5,
  input  in_6,
  input  in_7,
  input  in_8,
  input  in_9,
  input  in_10,
  input  in_11,
  input  in_12,
  input  in_13,
  input  in_14,
  input  in_15,
  input  in_16,
  output out_17,
  output out_18,
  output out_19,
  output out_20,
  output out_21,
  output out_22,
  output out_23,
  output out_24,
  output out_25
);

  wire nand_1_out, nand_2_out, nand_3_out, nand_4_out, nand_5_out, nand_8_out, nand_10_out, nor_1_out,
       nor_2_out, nor_3_out, nor_4_out, nor_5_out, nor_6_out, nor_7_out, nor_9_out, nor_10_out, nor_11_out,
       nor_12_out, nor_14_out;

  nor nor_1 (nor_1_out, in_6, in_6);
  nor nor_2 (nor_2_out, in_7, in_7);
  nor nor_3 (nor_3_out, in_8, in_8);
  nor nor_4 (nor_4_out, in_9, in_9);
  nor nor_5 (nor_5_out, in_2, in_3);
  nor nor_6 (nor_6_out, in_7, nor_1_out);
  nor nor_7 (nor_7_out, in_6, nor_2_out);
  nand nand_1 (nand_1_out, in_11, in_12);
  nand nand_2 (nand_2_out, in_15, in_15);
  nand nand_3 (nand_3_out, in_16, in_16);
  nor nor_8 (out_17, in_1, in_1);
  nor nor_9 (nor_9_out, in_4, in_4);
  nor nor_10 (nor_10_out, in_5, in_5);
  nor nor_11 (nor_11_out, in_9, nor_3_out);
  nor nor_12 (nor_12_out, in_8, nor_4_out);
  nand nand_4 (nand_4_out, in_13, in_13);
  nand nand_5 (nand_5_out, in_14, in_14);
  nor nor_13 (out_19, nor_9_out, nor_10_out);
  nor nor_14 (nor_14_out, nor_6_out, nor_7_out);
  nand nand_6 (out_22, in_10, in_10);
  nand nand_7 (out_24, nand_4_out, nand_5_out);
  nand nand_8 (nand_8_out, nand_3_out, in_15);
  nor nor_15 (out_18, nor_5_out, nor_5_out);
  nor nor_16 (out_21, nor_11_out, nor_12_out);
  nand nand_9 (out_23, nand_1_out, nand_1_out);
  nand nand_10 (nand_10_out, nand_2_out, in_16);
  nor nor_17 (out_20, nor_14_out, nor_14_out);
  nand nand_11 (out_25, nand_10_out, nand_8_out);

  // Notes on the sheet:
  //   Gates using NOR Gate
  //   Gates using NAND Gate
  //   NOT using NOR
  //   OR using NOR
  //   XNOR using NOR
  //   NOT using NAND
  //   XOR using NAND
  //   AND using NOR
  //   XOR using NOR
  //   AND using NAND
  //   OR using NAND
endmodule
